# Fritzing sketch MasterPost (saved by Fritzing 0.9.2b)
circuit board: 5.41963cm x 5.42cm
breadboards: 1

parts:
  PIC18LF4620 = PIC 16F877A [package=THT]
  Osc = Crystal [package=THT]
  Code_Load = SPST Switch [package=switch-spdt]
  I/O = female pin header, 2 pins [form="♀ (female)"]
  R1 = Resistor [tolerance=±5% resistance=1k package=THT]
  |+3V|GND| = female pin header, 2 pins [form="♀ (female)"]
  Reset = Momentary Switch [package=tactile-pth]
  R2 = Resistor [tolerance=±5% resistance=1k package=THT]
  U1 = PIC-ICSP [package=molex-1x6]
  U2 = PIC-ICSP [package=molex-1x6]
  ANT1 = Antenna
  R3 = Resistor [tolerance=±5% resistance=470 package=THT]
  C3 = Electrolytic Capacitor [capacitance=10µF package="100 mil [THT, electrolytic]"]
  R4 = Resistor [tolerance=±5% resistance=10 package=THT]
  R5 = Resistor [tolerance=±5% resistance=100 package=THT]
  R6 = Resistor [tolerance=±5% resistance=100 package=THT]
  C2 = Ceramic Capacitor [package="100 mil [THT, multilayer]"]
  C1 = Ceramic Capacitor [package="100 mil [THT, multilayer]"]

nets:
  N1: PIC18LF4620.MCLR, Reset.3, Reset.4, R2.Pin_1
  N2: PIC18LF4620.VDD, |+3V|GND|.pin1, R2.Pin_0, U1.RSSI, R4.Pin_1, R5.Pin_1
  VSS: PIC18LF4620.VSS, R1.Pin_1, |+3V|GND|.pin2, Reset.1, Reset.2, U1.NC, U2.GND, C3.+, C2.1, C1.0
  N3: PIC18LF4620.OSC1/CLKIN, Osc.pin_0, C2.0
  N4: PIC18LF4620.OSC2/CLKOUT, Osc.pin_1, C1.1
  N5: PIC18LF4620.RC6/TX/CK, I/O.pin2
  N6: PIC18LF4620.RC7/RX/DT, Code_Load.P, I/O.pin1
  N7: PIC18LF4620.RD7/PSP7, R6.Pin_1
  N8: Code_Load.O, R1.Pin_0
  N9: U1.RF, R3.Pin_0
  N10: U1.GND, R3.Pin_1, C3.-, R4.Pin_0
  N11: U1.A_REF, R5.Pin_0
  N12: U1.ANALOG, R6.Pin_0
  N13: U2.RF, ANT1.antenna_lead

notes:
  Carl
  Erik
  Cooper
  SD1522
  Master Post
  Carl Erik Cooper
  22pF

custom parts:
  PIC-ICSP: ISCP Programming connector for UAV, UBW Kit, etc.
  Ceramic Capacitor: 100 nF multilayer Ceramic Capacitor
