# Fritzing sketch WirelessController (saved by Fritzing 0.9.2b)
circuit board: 7.62cm x 7.62cm
breadboards: 1

parts:
  Reset = Momentary Switch [package=tactile-pth]
  Reset_2 = Resistor [tolerance=±5% resistance=1k package=THT]
  Transceiver_Pins_1-6 = PIC-ICSP [package=molex-1x6]
  Pins_7-12 = PIC-ICSP [package=molex-1x6]
  ANT1 = Antenna
  Osc = Crystal [package=THT]
  OscCap1 = Ceramic Capacitor [capacitance=100nF package="200 mil [THT, multilayer]"]
  OscCap2 = Ceramic Capacitor [capacitance=100nF package="200 mil [THT, multilayer]"]
  I/O = female pin header, 2 pins [form="♀ (female)"]
  MCP604 = OP482 - Low Power, High Speed JFET Quad Operational Amplifier [part_number=OP482]
  R4 = Resistor [tolerance=±5% resistance=1k package=THT]
  R7 = Resistor [tolerance=±5% resistance=470k package=THT]
  R8 = Resistor [tolerance=±5% resistance=3M package=THT]
  C2 = Ceramic Capacitor [capacitance=10nF package="100 mil [THT, multilayer]"]
  R9 = Resistor [tolerance=±5% resistance=2M package=THT]
  R10 = Resistor [tolerance=±5% resistance=2M package=THT]
  R-LED = LED - 5mm [color="Red (633nm)" package="5 mm [THT]"]
  R11 = Resistor [tolerance=±5% resistance=1k package=THT]
  R12 = Resistor [tolerance=±10% resistance=43k package=THT]
  R15 = Resistor [tolerance=±5% resistance=10 package=THT]
  C5 = Electrolytic Capacitor [capacitance=10µF package="100 mil [THT, electrolytic]"]
  R14 = Resistor [tolerance=±5% resistance=470 package=THT]
  Code_Load = SPST Switch [package=switch-spdt]
  PIC18LF4620 = ZIFSOCKET-40-6 [package=dil40-6-zif_socket]
  R13 = Resistor [tolerance=±5% resistance=10k package=THT]
  |3V|GND| = female pin header, 2 pins [form="♀ (female)"]
  C3 = Ceramic Capacitor [capacitance=100nF package="200 mil [THT, multilayer]"]
  C1 = Ceramic Capacitor [capacitance=100nF package="200 mil [THT, multilayer]"]
  C4 = Ceramic Capacitor [capacitance=100nF package="200 mil [THT, multilayer]"]
  RB0 = Momentary Switch [package=tactile-pth]
  RB1 = Momentary Switch [package=tactile-pth]
  RB0_2 = Resistor [tolerance=±5% resistance=1k package=THT]
  RB1_2 = Resistor [tolerance=±5% resistance=1k package=THT]
  Out = LED - 5mm [color="Red (633nm)" package="5 mm [THT]"]
  R16 = Resistor [tolerance=±5% resistance=1k package=THT]

nets:
  N1: Reset.1, Reset.2, Transceiver_Pins_1-6.PGC, Pins_7-12.PGD, Pins_7-12.VCC, OscCap1.1, OscCap2.1, MCP604.V-, R4.Pin_1, C2.0, R11.Pin_1, C5.-, PIC18LF4620.P$12, PIC18LF4620.P$31, R13.Pin_1, |3V|GND|.pin2, C4.0, RB0_2.Pin_1, RB1_2.Pin_1, Out.cathode
  N2: Reset.3, Reset.4, Reset_2.Pin_1, PIC18LF4620.P$1
  N3: Reset_2.Pin_0, Pins_7-12.GND, MCP604.V+, R12.Pin_0, R15.Pin_1, PIC18LF4620.P$11, PIC18LF4620.P$32, |3V|GND|.pin1, RB0.3, RB0.4, RB1.3, RB1.4
  N4: Transceiver_Pins_1-6.PGM, ANT1.antenna_lead
  N5: Transceiver_Pins_1-6.GND, PIC18LF4620.P$2
  N6: Pins_7-12.PGM, R14.Pin_0
  N7: Pins_7-12.PGC, R15.Pin_0, C5.+, R14.Pin_1
  N8: Pins_7-12.VPP, R7.Pin_0
  N9: Osc.pin_0, OscCap1.0, PIC18LF4620.P$14
  N10: Osc.pin_1, OscCap2.0, PIC18LF4620.P$13
  N11: I/O.pin1, Code_Load.P, PIC18LF4620.P$26
  N12: I/O.pin2, PIC18LF4620.P$25
  N13: MCP604.OUTA, PIC18LF4620.P$35
  N14: MCP604.-INA, R12.Pin_1, R13.Pin_0
  N15: MCP604.+INA, R-LED.cathode, R11.Pin_0
  N16: MCP604.OUTC, MCP604.-INC, R9.Pin_0, C1.1
  N17: MCP604.+INC, R8.Pin_1, C2.1
  N18: MCP604.+IND, R10.Pin_0, C4.1
  N19: MCP604.-IND, MCP604.OUTD, R-LED.anode, C3.1
  N20: R4.Pin_0, Code_Load.O
  N21: R7.Pin_1, R8.Pin_0, C1.0
  N22: R9.Pin_1, R10.Pin_1, C3.0
  N23: PIC18LF4620.P$30, R16.Pin_0
  N24: PIC18LF4620.P$33, RB0.1, RB0.2, RB0_2.Pin_0
  N25: PIC18LF4620.P$34, RB1.1, RB1.2, RB1_2.Pin_0
  N26: Out.anode, R16.Pin_1

notes:
  TRM-418-LT
  Wireless Controller
  Carl Erik Cooper
  SD1522
  22pF
  100nF
  820pF

custom parts:
  Ceramic Capacitor: 100 nF multilayer Ceramic Capacitor
